# Fritzing sketch ESP32_Connections (saved by Fritzing 0.9.4)
breadboards: 2

parts:
  U1 = LCD-16X2 [package=lcd-16x2_noholes]
  LED1 = smd LED [color="Red (633nm)" package="0805 [SMD]"]
  Part1 = Passive Buzzer
  U3 = ESP32-38PinWide [part_number=ESP32-38PinWide]
  R1 = Resistor [tolerance=±5% resistance=10k package=THT]
  S1 = KY-026

nets:
  VSS: U1.VSS, U1.R_W, U1.K, LED1.cathode, U3.GND, R1.Pin_0, S1.pin2
  VDD: U1.VDD, U1.A, Part1.NC, U3.VIN, S1.pin3
  N1: U1.VO, R1.Pin_1
  N2: U1.RS, U3.GPIO19
  N3: U1.E, U3.GPIO23
  N4: U1.DB4, U3.GPIO18
  N5: U1.DB5, U3.GPIO17
  N6: U1.DB6, U3.GPIO16
  N7: U1.DB7, U3.GPIO15
  N8: LED1.anode, U3.GPIO12
  N9: Part1.S, U3.GPIO21
  N10: U3.GPIO8, S1.pin4

custom parts:
  ESP32-38PinWide: Generic 38-Pin ESP32 with wide format (only access to one side of pins on a breadboard) based on Stephen Lilley's HiLetgo ESP-WROOM-32 ESP32 ESP-32S Development Board.
  KY-026: ky-026 flame sensor module

// code stored in the sketch: Untitled.ino

